// Logisim project input.circ as structural Verilog: 2 circuits, main circuit main
module main (
  input  [2:0] in_1
);

  wire Runway_Status_runway_a_status, Runway_Status_runway_b_status, Runway_Status_wait_signal;
  wire [2:1] d_ff_2_q;
  wire [3:0] Runway_Picker_o4_o3_o2_o1;

  runway_picker Runway_Picker (.D1_D2_A_B_En({in_1[2:1], d_ff_2_q, in_1[0]}), .O4_O3_O2_O1(Runway_Picker_o4_o3_o2_o1));
  LED Wait_For_Landing (.in(Runway_Status_wait_signal));
  D_Flip_Flop d_ff_1 (
    .clk(in_1[0]), .D(Runway_Status_runway_a_status), .Q(d_ff_2_q[2]));  // open: Qn, preset, en, reset
  D_Flip_Flop d_ff_2 (
    .clk(in_1[0]), .D(Runway_Status_runway_b_status), .Q(d_ff_2_q[1]));  // open: Qn, preset, en, reset
  LED led_1 (.in(Runway_Status_runway_b_status));
  LED led_2 (.in(Runway_Status_runway_a_status));
  runway_status_main Runway_Status (
    .Runway_B_Status(Runway_Status_runway_b_status), .Runway_A_Status(Runway_Status_runway_a_status),
    .Wait_signal(Runway_Status_wait_signal), .in_1({Runway_Picker_o4_o3_o2_o1, in_1[0]}));
endmodule

module runway_picker (
  input  [4:0] D1_D2_A_B_En,
  output [3:0] O4_O3_O2_O1
);

  wire and_1_out, and_2_out, not_1_out, not_2_out, not_3_out, or_1_out;

  and and_1 (and_1_out, D1_D2_A_B_En[1], D1_D2_A_B_En[2]);
  not not_1 (not_1_out, D1_D2_A_B_En[1]);
  not not_2 (not_2_out, D1_D2_A_B_En[3]);
  and and_2 (and_2_out, not_1_out, not_2_out);
  not not_3 (not_3_out, and_1_out);
  or or_1 (or_1_out, D1_D2_A_B_En[2], and_2_out);
  and and_3 (O4_O3_O2_O1[3], D1_D2_A_B_En[0], 1'b1);
  and and_4 (O4_O3_O2_O1[2], D1_D2_A_B_En[0], and_1_out);
  and and_5 (O4_O3_O2_O1[1], D1_D2_A_B_En[0], not_3_out);
  and and_6 (O4_O3_O2_O1[0], D1_D2_A_B_En[0], or_1_out);

  // Notes on the sheet:
  //   Runway Picker
  //   O4 = 1
  //   O3 = A.B
  //   O2 = (A.B)'
  //   O1 = A + B'.D2'
endmodule
