// Logisim project input.circ as structural Verilog: 1 circuit, main circuit main
module main (
  input  [1:0] Direction,
  input  in_2,
  input  in_3,
  input  [3:0] in_4
);

  wire clock_1_out, Runway_status_runway_a_status, Runway_status_runway_b_status;
  wire [1:0] register_1_q, Runway_Picker_out_6;

  runway_picker_main Runway_Picker (
    .Direction_1(Direction[0]), .Direction_2(Direction[1]), .Runway_A_status(in_2), .Runway_B_status(in_3),
    .out_5(Runway_Picker_out_6[1]), .out_6(Runway_Picker_out_6[0]));
  runway_status_main Runway_status (
    .Runway_B_status(Runway_status_runway_b_status), .Runway_A_status(Runway_status_runway_a_status),
    .in_1(in_4));
  Register #(.width(2)) register_1 (.D(Runway_Picker_out_6), .Q(register_1_q), .clk(clock_1_out));  // open: en, clr
  Clock clock_1 (.out(clock_1_out));
endmodule
