// Logisim project runway_status.circ as structural Verilog: 1 circuit, main circuit main
module main (
  input  [1:0] Chosen_Runway,
  output Runway_B_status,
  output Runway_A_status
);

  wire clock_1_out, counter_1_carry, counter_2_carry, demultiplexer_1_out0, demultiplexer_1_out1, not_1_out,
       not_2_out, not_3_out, not_4_out;

  Demultiplexer #(.select(2)) demultiplexer_1 (
    .out0(demultiplexer_1_out0), .out1(demultiplexer_1_out1), .in(1'b1), .sel(Chosen_Runway));  // open: out2, out3, en
  Clock clock_1 (.out(clock_1_out));
  and and_1 (Runway_A_status, demultiplexer_1_out0, not_2_out);
  Counter #(.width(4), .max('hd), .ongoal("stay")) counter_1 (
    .carry(counter_1_carry), .clk(clock_1_out), .clr(not_1_out));  // open: load, D, count, Q
  not not_1 (not_1_out, demultiplexer_1_out0);
  and and_2 (Runway_B_status, demultiplexer_1_out1, not_4_out);
  not not_2 (not_2_out, counter_1_carry);
  Counter #(.width(4), .max('hd), .ongoal("stay")) counter_2 (
    .carry(counter_2_carry), .clk(clock_1_out), .clr(not_3_out));  // open: load, D, count, Q
  not not_3 (not_3_out, demultiplexer_1_out1);
  not not_4 (not_4_out, counter_2_carry);

  // Notes on the sheet:
  //   00 for A, 01 for B
endmodule
